// Logisim project 4bit_sort.circ as structural Verilog: 3 circuits, main circuit 1bit_swap
module _1bit_swap (
  input  A,
  input  B,
  input  C,
  output O1,
  output O2
);

  wire and_1_out, and_2_out, and_3_out, and_4_out, not_1_out, not_2_out;

  not not_1 (not_1_out, C);
  not not_2 (not_2_out, C);
  and and_1 (and_1_out, B, C);
  and and_2 (and_2_out, A, not_1_out);
  and and_3 (and_3_out, B, not_2_out);
  and and_4 (and_4_out, A, C);
  or or_1 (O1, and_1_out, and_2_out);
  or or_2 (O2, and_3_out, and_4_out);
endmodule

module _4bit_swap (
  input  [3:0] A,
  input  [3:0] B,
  input  ENA,
  output [3:0] O1,
  output [3:0] _02
);

  _1bit_swap u_1bit_swap_1 (.A(A[0]), .B(B[0]), .C(ENA), .O1(O1[0]), .O2(_02[0]));
  _1bit_swap u_1bit_swap_2 (.A(A[1]), .B(B[1]), .C(ENA), .O1(O1[1]), .O2(_02[1]));
  _1bit_swap u_1bit_swap_3 (.A(A[2]), .B(B[2]), .C(ENA), .O1(O1[2]), .O2(_02[2]));
  _1bit_swap u_1bit_swap_4 (.A(A[3]), .B(B[3]), .C(ENA), .O1(O1[3]), .O2(_02[3]));

  // Other names for the same wires on the sheet: O2_0 = _02[0]; O2_1 = _02[1]; O2_2 = _02[2]; O2_3 = _02[3];
  //   A_0 = A[0]; A_1 = A[1]; A_2 = A[2]; A_3 = A[3]; B_0 = B[0]; B_1 = B[1]; B_2 = B[2]; B_3 = B[3]; E_0 = ENA;
  //   O1_0 = O1[0]; O1_1 = O1[1]; O1_2 = O1[2]; O1_3 = O1[3]
endmodule

module _4bit_sort (
  input  [3:0] in0,
  input  [3:0] in1,
  input  [3:0] in2,
  input  [3:0] in3,
  output [3:0] out0,
  output [3:0] out1,
  output [3:0] out2,
  output [3:0] out3
);

  wire comparator_1_gt, comparator_2_gt, comparator_3_gt, comparator_4_gt, comparator_5_gt;
  wire [3:0] bigger_0, bigger_1, n4bit_swap_3__02, n4bit_swap_4_o1, smaller_0, smaller_1;

  // Probe on in0
  // Probe on in0
  _4bit_swap u_4bit_swap_1 (.A(in0), .B(in1), .ENA(comparator_1_gt), .O1(smaller_0), ._02(bigger_0));
  Comparator #(.width(4), .mode("unsigned")) comparator_1 (.a(in0), .b(in1), .gt(comparator_1_gt));  // open: eq, lt
  _4bit_swap u_4bit_swap_2 (.A(in2), .B(in3), .ENA(comparator_2_gt), .O1(smaller_1), ._02(bigger_1));
  Comparator #(.width(4), .mode("unsigned")) comparator_2 (.a(in2), .b(in3), .gt(comparator_2_gt));  // open: eq, lt
  _4bit_swap u_4bit_swap_3 (.A(smaller_0), .B(smaller_1), .ENA(comparator_3_gt), .O1(out0), ._02(n4bit_swap_3__02));
  Comparator #(.width(4), .mode("unsigned")) comparator_3 (
    .a(smaller_0), .b(smaller_1), .gt(comparator_3_gt));  // open: eq, lt
  _4bit_swap u_4bit_swap_4 (.A(bigger_0), .B(bigger_1), .ENA(comparator_4_gt), .O1(n4bit_swap_4_o1), ._02(out3));
  Comparator #(.width(4), .mode("unsigned")) comparator_4 (
    .a(bigger_0), .b(bigger_1), .gt(comparator_4_gt));  // open: eq, lt
  // Probe on comparator_1_gt
  _4bit_swap u_4bit_swap_5 (.A(n4bit_swap_3__02), .B(n4bit_swap_4_o1), .ENA(comparator_5_gt), .O1(out1), ._02(out2));
  Comparator #(.width(4), .mode("unsigned")) comparator_5 (
    .a(n4bit_swap_3__02), .b(n4bit_swap_4_o1), .gt(comparator_5_gt));  // open: eq, lt

  // Other names for the same wires on the sheet: in_0[3:0] = in0; in_1[3:0] = in1; in_2[3:0] = in2; in_3[3:0] = in3;
  //   out_0[3:0] = out0; out_1[3:0] = out1; out_2[3:0] = out2; out_3[3:0] = out3

  // Notes on the sheet:
  //   Merge Sort
endmodule
