// Logisim project CRC.circ as structural Verilog
module mod2divider (
  input  [3:0] X,
  input  [3:0] Y,
  output Q,
  output [2:0] R
);

  wire [2:0] \xor ;

  xor xor_1 (\xor [2], X[2], Y[2]);
  xor xor_2 (\xor [1], X[1], Y[1]);
  xor xor_3 (\xor [0], X[0], Y[0]);
  Multiplexer #(.width(3)) multiplexer_1 (.in0(X[2:0]), .in1(\xor ), .out(R), .sel(X[3]));  // open: en

  assign Q = X[0];

  // Other names for the same wires on the sheet: lower_x[2:0] = X[2:0]
endmodule

module CRC (
  input  [7:0] A,
  input  [3:0] B,
  output [10:0] C
);

  wire [2:0] mod2divider_1_r, mod2divider_2_r, mod2divider_3_r, mod2divider_4_r, mod2divider_5_r,
       mod2divider_7_r, r1;

  // Probe on A[7:4]
  // Probe on mod2divider_1_r
  mod2divider mod2divider_1 (.X(A[7:4]), .Y(B), .R(mod2divider_1_r));  // open: Q
  mod2divider mod2divider_2 (.X({r1, 1'b0}), .Y(B), .R(mod2divider_2_r));  // open: Q
  // Probe on {mod2divider_1_r, A[3]}
  mod2divider mod2divider_3 (.X({mod2divider_1_r, A[3]}), .Y(B), .R(mod2divider_3_r));  // open: Q
  // Probe on mod2divider_3_r
  mod2divider mod2divider_4 (.X({mod2divider_2_r, 1'b0}), .Y(B), .R(mod2divider_4_r));  // open: Q
  // Probe on {mod2divider_3_r, A[2]}
  mod2divider mod2divider_5 (.X({mod2divider_3_r, A[2]}), .Y(B), .R(mod2divider_5_r));  // open: Q
  // Probe on mod2divider_5_r
  mod2divider mod2divider_6 (.X({mod2divider_4_r, 1'b0}), .Y(B), .R(C[2:0]));  // open: Q
  mod2divider mod2divider_7 (.X({mod2divider_5_r, A[1]}), .Y(B), .R(mod2divider_7_r));  // open: Q
  // Probe on mod2divider_7_r
  mod2divider mod2divider_8 (.X({mod2divider_7_r, A[0]}), .Y(B), .R(r1));  // open: Q

  assign C[10:3] = A;

  // Other names for the same wires on the sheet: code[2:0] = C[2:0]; in[7:0] = A; divider[3:0] = B
endmodule
