// Logisim project CT74161.circ as structural Verilog: 1 circuit, main circuit main
module main (
  input  Q0,
  input  Q1,
  input  Q2,
  input  Q3,
  input  C,
  input  in_6,
  output Q0_prime,
  output Q1_prime,
  output Q2_prime,
  output Q3_prime,
  output EP,
  output nLD,
  output ET,
  output CP,
  output nRD,
  output D0,
  output D1,
  output D2,
  output D3
);

  wire not_4_out;

  Clock clock_1 (.out(CP));
  xnor xnor_1 (Q3_prime, Q2, Q3);
  not not_1 (Q2_prime, Q2);
  not not_2 (nLD, not_4_out);
  not not_3 (nRD, in_6);
  not not_4 (not_4_out, C);

  assign D0 = 1'b0;
  assign D1 = 1'b0;
  assign D2 = 1'b1;
  assign D3 = 1'b0;
  assign EP = 1'b1;
  assign ET = 1'b1;
  assign Q0_prime = Q0;
  assign Q1_prime = Q1;

  // Notes on the sheet:
  //   CT74161
endmodule
