// Logisim project GRF.circ as structural Verilog: 1 circuit, main circuit grf
module grf (
);

  wire and_1_out, clk, reset, Sel0, WE;
  wire [31:0] inData, multiplexer_1_out, O0;

  Register #(.width(32)) _0 (.D(multiplexer_1_out), .Q(O0), .clk(clk), .clr(reset));  // open: en
  Multiplexer #(.width(32)) multiplexer_1 (
    .in0(O0), .in1(inData), .out(multiplexer_1_out), .sel(and_1_out));  // open: en
  and and_1 (and_1_out, WE, Sel0);
endmodule
