// Logisim project GRF_1.circ as structural Verilog: 1 circuit, main circuit grf
module grf (
  input  WE,
  input  [4:0] A1,
  input  [4:0] A2,
  input  [4:0] A3,
  input  [31:0] WD,
  input  clk,
  input  reset,
  output [31:0] RD1,
  output [31:0] RD2
);

  wire and_1_out, and_2_out, and_3_out, and_4_out, and_5_out, and_6_out, and_7_out, and_8_out, and_9_out,
       and_10_out, and_11_out, and_12_out, and_13_out, and_14_out, and_15_out, and_16_out, and_17_out,
       and_18_out, and_19_out, and_20_out, and_21_out, and_22_out, and_23_out, and_24_out, and_25_out,
       and_26_out, and_27_out, and_28_out, and_29_out, and_30_out, and_31_out, and_32_out, Sel0, Sel1, Sel2,
       Sel3, Sel4, Sel5, Sel6, Sel7, Sel8, Sel9, Sel10, Sel11, Sel12, Sel13, Sel14, Sel15, Sel16, Sel17,
       Sel18, Sel19, Sel20, Sel21, Sel22, Sel23, Sel24, Sel25, Sel26, Sel27, Sel28, Sel29, Sel30, Sel31;
  wire [31:0] multiplexer_1_out, multiplexer_2_out, multiplexer_3_out, multiplexer_4_out, multiplexer_5_out,
       multiplexer_6_out, multiplexer_7_out, multiplexer_8_out, multiplexer_9_out, multiplexer_10_out,
       multiplexer_11_out, multiplexer_12_out, multiplexer_13_out, multiplexer_14_out, multiplexer_15_out,
       multiplexer_16_out, multiplexer_17_out, multiplexer_18_out, multiplexer_19_out, multiplexer_20_out,
       multiplexer_21_out, multiplexer_22_out, multiplexer_23_out, multiplexer_24_out, multiplexer_25_out,
       multiplexer_26_out, multiplexer_27_out, multiplexer_28_out, multiplexer_29_out, multiplexer_30_out,
       multiplexer_31_out, multiplexer_32_out, O0, O1, O2, O3, O4, O5, O6, O7, O8, O9, O10, O11, O12, O13,
       O14, O15, O16, O17, O18, O19, O20, O21, O22, O23, O24, O25, O26, O27, O28, O29, O30, O31;

  Register #(.width(32)) _0 (.D(multiplexer_1_out), .Q(O0), .clk(clk), .clr(reset));  // open: en
  Multiplexer #(.width(32)) multiplexer_1 (.in0(O0), .in1(WD), .out(multiplexer_1_out), .sel(and_1_out));  // open: en
  and and_1 (and_1_out, WE, 1'b0, Sel0);
  Multiplexer #(.width(32)) multiplexer_2 (.in0(O1), .in1(WD), .out(multiplexer_2_out), .sel(and_2_out));  // open: en
  Register #(.width(32)) _1 (.D(multiplexer_2_out), .Q(O1), .clk(clk), .clr(reset));  // open: en
  and and_2 (and_2_out, WE, Sel1);
  Multiplexer #(.width(32)) multiplexer_3 (.in0(O2), .in1(WD), .out(multiplexer_3_out), .sel(and_3_out));  // open: en
  Register #(.width(32)) _2 (.D(multiplexer_3_out), .Q(O2), .clk(clk), .clr(reset));  // open: en
  and and_3 (and_3_out, WE, Sel2);
  Register #(.width(32)) _3 (.D(multiplexer_4_out), .Q(O3), .clk(clk), .clr(reset));  // open: en
  Multiplexer #(.width(32)) multiplexer_4 (.in0(O3), .in1(WD), .out(multiplexer_4_out), .sel(and_4_out));  // open: en
  and and_4 (and_4_out, WE, Sel3);
  Register #(.width(32)) _4 (.D(multiplexer_5_out), .Q(O4), .clk(clk), .clr(reset));  // open: en
  Multiplexer #(.width(32)) multiplexer_5 (.in0(O4), .in1(WD), .out(multiplexer_5_out), .sel(and_5_out));  // open: en
  and and_5 (and_5_out, WE, Sel4);
  Multiplexer #(.width(32)) multiplexer_6 (.in0(O5), .in1(WD), .out(multiplexer_6_out), .sel(and_6_out));  // open: en
  Register #(.width(32)) _5 (.D(multiplexer_6_out), .Q(O5), .clk(clk), .clr(reset));  // open: en
  and and_6 (and_6_out, WE, Sel5);
  Register #(.width(32)) _6 (.D(multiplexer_7_out), .Q(O6), .clk(clk), .clr(reset));  // open: en
  Multiplexer #(.width(32)) multiplexer_7 (.in0(O6), .in1(WD), .out(multiplexer_7_out), .sel(and_7_out));  // open: en
  and and_7 (and_7_out, WE, Sel6);
  Multiplexer #(.width(32)) multiplexer_8 (.in0(O7), .in1(WD), .out(multiplexer_8_out), .sel(and_8_out));  // open: en
  Register #(.width(32)) _7 (.D(multiplexer_8_out), .Q(O7), .clk(clk), .clr(reset));  // open: en
  and and_8 (and_8_out, WE, Sel7);
  Multiplexer #(.width(32)) multiplexer_9 (.in0(O8), .in1(WD), .out(multiplexer_9_out), .sel(and_9_out));  // open: en
  and and_9 (and_9_out, WE, Sel8);
  Multiplexer #(.width(32)) multiplexer_10 (
    .in0(O9), .in1(WD), .out(multiplexer_10_out), .sel(and_10_out));  // open: en
  and and_10 (and_10_out, WE, Sel9);
  Multiplexer #(.width(32)) multiplexer_11 (
    .in0(O10), .in1(WD), .out(multiplexer_11_out), .sel(and_11_out));  // open: en
  and and_11 (and_11_out, WE, Sel10);
  Multiplexer #(.width(32)) multiplexer_12 (
    .in0(O11), .in1(WD), .out(multiplexer_12_out), .sel(and_12_out));  // open: en
  and and_12 (and_12_out, WE, Sel11);
  Multiplexer #(.width(32)) multiplexer_13 (
    .in0(O12), .in1(WD), .out(multiplexer_13_out), .sel(and_13_out));  // open: en
  and and_13 (and_13_out, WE, Sel12);
  Multiplexer #(.width(32)) multiplexer_14 (
    .in0(O13), .in1(WD), .out(multiplexer_14_out), .sel(and_14_out));  // open: en
  and and_14 (and_14_out, WE, Sel13);
  Multiplexer #(.width(32)) multiplexer_15 (
    .in0(O14), .in1(WD), .out(multiplexer_15_out), .sel(and_15_out));  // open: en
  and and_15 (and_15_out, WE, Sel14);
  Multiplexer #(.width(32)) multiplexer_16 (
    .in0(O15), .in1(WD), .out(multiplexer_16_out), .sel(and_16_out));  // open: en
  and and_16 (and_16_out, WE, Sel15);
  Register #(.width(32)) _8 (.D(multiplexer_9_out), .Q(O8), .clk(clk), .clr(reset));  // open: en
  Register #(.width(32)) _9 (.D(multiplexer_10_out), .Q(O9), .clk(clk), .clr(reset));  // open: en
  Register #(.width(32)) _10 (.D(multiplexer_11_out), .Q(O10), .clk(clk), .clr(reset));  // open: en
  Register #(.width(32)) _11 (.D(multiplexer_12_out), .Q(O11), .clk(clk), .clr(reset));  // open: en
  Register #(.width(32)) _12 (.D(multiplexer_13_out), .Q(O12), .clk(clk), .clr(reset));  // open: en
  Register #(.width(32)) _13 (.D(multiplexer_14_out), .Q(O13), .clk(clk), .clr(reset));  // open: en
  Register #(.width(32)) _14 (.D(multiplexer_15_out), .Q(O14), .clk(clk), .clr(reset));  // open: en
  Register #(.width(32)) _15 (.D(multiplexer_16_out), .Q(O15), .clk(clk), .clr(reset));  // open: en
  Multiplexer #(.width(32)) multiplexer_17 (
    .in0(O16), .in1(WD), .out(multiplexer_17_out), .sel(and_17_out));  // open: en
  and and_17 (and_17_out, WE, Sel16);
  Multiplexer #(.width(32)) multiplexer_18 (
    .in0(O17), .in1(WD), .out(multiplexer_18_out), .sel(and_18_out));  // open: en
  and and_18 (and_18_out, WE, Sel17);
  Multiplexer #(.width(32)) multiplexer_19 (
    .in0(O18), .in1(WD), .out(multiplexer_19_out), .sel(and_19_out));  // open: en
  and and_19 (and_19_out, WE, Sel18);
  Multiplexer #(.width(32)) multiplexer_20 (
    .in0(O19), .in1(WD), .out(multiplexer_20_out), .sel(and_20_out));  // open: en
  and and_20 (and_20_out, WE, Sel19);
  Multiplexer #(.width(32)) multiplexer_21 (
    .in0(O20), .in1(WD), .out(multiplexer_21_out), .sel(and_21_out));  // open: en
  and and_21 (and_21_out, WE, Sel20);
  Multiplexer #(.width(32)) multiplexer_22 (
    .in0(O21), .in1(WD), .out(multiplexer_22_out), .sel(and_22_out));  // open: en
  and and_22 (and_22_out, WE, Sel21);
  Multiplexer #(.width(32)) multiplexer_23 (
    .in0(O22), .in1(WD), .out(multiplexer_23_out), .sel(and_23_out));  // open: en
  and and_23 (and_23_out, WE, Sel22);
  Multiplexer #(.width(32)) multiplexer_24 (
    .in0(O23), .in1(WD), .out(multiplexer_24_out), .sel(and_24_out));  // open: en
  and and_24 (and_24_out, WE, Sel23);
  Register #(.width(32)) _16 (.D(multiplexer_17_out), .Q(O16), .clk(clk), .clr(reset));  // open: en
  Register #(.width(32)) _17 (.D(multiplexer_18_out), .Q(O17), .clk(clk), .clr(reset));  // open: en
  Register #(.width(32)) _18 (.D(multiplexer_19_out), .Q(O18), .clk(clk), .clr(reset));  // open: en
  Register #(.width(32)) _19 (.D(multiplexer_20_out), .Q(O19), .clk(clk), .clr(reset));  // open: en
  Register #(.width(32)) _20 (.D(multiplexer_21_out), .Q(O20), .clk(clk), .clr(reset));  // open: en
  Register #(.width(32)) _21 (.D(multiplexer_22_out), .Q(O21), .clk(clk), .clr(reset));  // open: en
  Register #(.width(32)) _22 (.D(multiplexer_23_out), .Q(O22), .clk(clk), .clr(reset));  // open: en
  Register #(.width(32)) _23 (.D(multiplexer_24_out), .Q(O23), .clk(clk), .clr(reset));  // open: en
  Multiplexer #(.width(32)) multiplexer_25 (
    .in0(O24), .in1(WD), .out(multiplexer_25_out), .sel(and_25_out));  // open: en
  and and_25 (and_25_out, WE, Sel24);
  Multiplexer #(.width(32)) multiplexer_26 (
    .in0(O25), .in1(WD), .out(multiplexer_26_out), .sel(and_26_out));  // open: en
  and and_26 (and_26_out, WE, Sel25);
  Multiplexer #(.width(32)) multiplexer_27 (
    .in0(O26), .in1(WD), .out(multiplexer_27_out), .sel(and_27_out));  // open: en
  and and_27 (and_27_out, WE, Sel26);
  Multiplexer #(.width(32)) multiplexer_28 (
    .in0(O27), .in1(WD), .out(multiplexer_28_out), .sel(and_28_out));  // open: en
  and and_28 (and_28_out, WE, Sel27);
  Multiplexer #(.width(32)) multiplexer_29 (
    .in0(O28), .in1(WD), .out(multiplexer_29_out), .sel(and_29_out));  // open: en
  and and_29 (and_29_out, WE, Sel28);
  Multiplexer #(.width(32)) multiplexer_30 (
    .in0(O29), .in1(WD), .out(multiplexer_30_out), .sel(and_30_out));  // open: en
  and and_30 (and_30_out, WE, Sel29);
  Multiplexer #(.width(32)) multiplexer_31 (
    .in0(O30), .in1(WD), .out(multiplexer_31_out), .sel(and_31_out));  // open: en
  and and_31 (and_31_out, WE, Sel30);
  Multiplexer #(.width(32)) multiplexer_32 (
    .in0(O31), .in1(WD), .out(multiplexer_32_out), .sel(and_32_out));  // open: en
  and and_32 (and_32_out, WE, Sel31);
  Register #(.width(32)) _24 (.D(multiplexer_25_out), .Q(O24), .clk(clk), .clr(reset));  // open: en
  Register #(.width(32)) _25 (.D(multiplexer_26_out), .Q(O25), .clk(clk), .clr(reset));  // open: en
  Register #(.width(32)) _26 (.D(multiplexer_27_out), .Q(O26), .clk(clk), .clr(reset));  // open: en
  Register #(.width(32)) _27 (.D(multiplexer_28_out), .Q(O27), .clk(clk), .clr(reset));  // open: en
  Register #(.width(32)) _28 (.D(multiplexer_29_out), .Q(O28), .clk(clk), .clr(reset));  // open: en
  Register #(.width(32)) _29 (.D(multiplexer_30_out), .Q(O29), .clk(clk), .clr(reset));  // open: en
  Register #(.width(32)) _30 (.D(multiplexer_31_out), .Q(O30), .clk(clk), .clr(reset));  // open: en
  Register #(.width(32)) _31 (.D(multiplexer_32_out), .Q(O31), .clk(clk), .clr(reset));  // open: en
  Multiplexer #(.select(5), .width(32)) multiplexer_33 (
    .in0(O0), .in1(O1), .in2(O2), .in3(O3), .in4(O4), .in5(O5), .in6(O6), .in7(O7), .in8(O8), .in9(O9),
    .in10(O10), .in11(O11), .in12(O12), .in13(O13), .in14(O14), .in15(O15), .in16(O16), .in17(O17),
    .in18(O18), .in19(O19), .in20(O20), .in21(O21), .in22(O22), .in23(O23), .in24(O24), .in25(O25),
    .in26(O26), .in27(O27), .in28(O28), .in29(O29), .in30(O30), .in31(O31), .out(RD1), .sel(A1));  // open: en
  Multiplexer #(.select(5), .width(32)) multiplexer_34 (
    .in0(O0), .in1(O1), .in2(O2), .in3(O3), .in4(O4), .in5(O5), .in6(O6), .in7(O7), .in8(O8), .in9(O9),
    .in10(O10), .in11(O11), .in12(O12), .in13(O13), .in14(O14), .in15(O15), .in16(O16), .in17(O17),
    .in18(O18), .in19(O19), .in20(O20), .in21(O21), .in22(O22), .in23(O23), .in24(O24), .in25(O25),
    .in26(O26), .in27(O27), .in28(O28), .in29(O29), .in30(O30), .in31(O31), .out(RD2), .sel(A2));  // open: en
  Demultiplexer #(.select(5)) demultiplexer_1 (
    .out0(Sel0), .out1(Sel1), .out2(Sel2), .out3(Sel3), .out4(Sel4), .out5(Sel5), .out6(Sel6), .out7(Sel7),
    .out8(Sel8), .out9(Sel9), .out10(Sel10), .out11(Sel11), .out12(Sel12), .out13(Sel13), .out14(Sel14),
    .out15(Sel15), .out16(Sel16), .out17(Sel17), .out18(Sel18), .out19(Sel19), .out20(Sel20), .out21(Sel21),
    .out22(Sel22), .out23(Sel23), .out24(Sel24), .out25(Sel25), .out26(Sel26), .out27(Sel27), .out28(Sel28),
    .out29(Sel29), .out30(Sel30), .out31(Sel31), .in(1'b1), .sel(A3));  // open: en

  // Other names for the same wires on the sheet: inData[31:0] = WD
endmodule
