// Logisim project Mealy_fsm.circ as structural Verilog
module fsm (
  input  CLR,
  input  [1:0] In,
  output Z
);

  wire CLK, I1, I2, nIn0, nIn1, not_3_out, not_4_out, O0, O1, O2;
  wire [1:0] multiplexer_1_out;

  not not_1 (nIn1, In[1]);
  not not_2 (nIn0, In[0]);
  Clock clock_1 (.out(CLK));
  and and_1 (I1, nIn1, In[0]);
  and and_2 (I2, O1, nIn0);
  Multiplexer #(.width(2)) multiplexer_1 (.in0({I2, I1}), .in1(2'b00), .out(multiplexer_1_out), .sel(CLR));  // open: en
  Register #(.width(2)) register_1 (.D(multiplexer_1_out), .Q({O2, O1}), .clk(CLK));  // open: en, clr
  not not_3 (not_3_out, O1);
  not not_4 (not_4_out, O2);
  and and_3 (O0, not_3_out, not_4_out);
  and and_4 (Z, O2, nIn0);
endmodule
