// Logisim project fib_4.circ as structural Verilog: 1 circuit, main circuit main
module main (
  input  [2:0] N,
  output [3:0] out_2
);

  wire clk, comparator_1_eq, comparator_2_eq;
  wire [2:0] counter_1_q;
  wire [3:0] adder_1_out, multiplexer_1_out, register_1_q, register_2_q, register_3_q;

  Counter #(.width(3), .max('h7)) counter_1 (.Q(counter_1_q));  // open: load, D, count, carry, clk, clr
  Comparator #(.width(3)) comparator_1 (.a(counter_1_q), .b(3'b000), .eq(comparator_1_eq));  // open: gt, lt
  Clock clock_1 (.out(clk));
  Comparator #(.width(3)) comparator_2 (.a(N), .b(counter_1_q), .eq(comparator_2_eq));  // open: gt, lt
  Multiplexer #(.width(4)) multiplexer_1 (
    .in0(register_3_q), .in1(4'b0001), .out(multiplexer_1_out), .sel(comparator_1_eq));  // open: en
  Register #(.width(4)) register_1 (.D(register_2_q), .Q(register_1_q));  // open: en, clk, clr
  Register #(.width(4)) register_2 (.D(multiplexer_1_out), .Q(register_2_q));  // open: en, clk, clr
  Register #(.width(4)) register_3 (.D(adder_1_out), .Q(register_3_q));  // open: en, clk, clr
  Adder #(.width(4)) adder_1 (.a(register_1_q), .b(register_2_q), .out(adder_1_out));  // open: cin, cout
  Multiplexer #(.width(4)) multiplexer_2 (
    .in0(4'b0000), .in1(register_1_q), .out(out_2), .sel(comparator_2_eq));  // open: en
endmodule
