// Logisim project fib_4_new.circ as structural Verilog: 1 circuit, main circuit main
module main (
  input  [2:0] in_1,
  output [3:0] out_2
);

  wire CLK, eq, zero;
  wire [2:0] CLK_res;
  wire [3:0] add_res, former, latter, multiplexer_1_out;

  // Probe on CLK_res
  Counter #(.width(3), .max('h7)) counter_1 (.Q(CLK_res), .clk(CLK));  // open: load, D, count, carry, clr
  Clock clock_1 (.out(CLK));
  Multiplexer #(.width(4)) multiplexer_1 (
    .in0(add_res), .in1(4'b0001), .out(multiplexer_1_out), .sel(zero));  // open: en
  Register #(.width(4)) register_1 (.D(multiplexer_1_out), .Q(former), .clk(CLK), .clr(eq));  // open: en
  Adder #(.width(4)) adder_1 (.a(latter), .b(former), .out(add_res));  // open: cin, cout
  Comparator #(.width(3)) comparator_1 (.a(CLK_res), .b(3'b000), .eq(zero));  // open: gt, lt
  Register #(.width(4)) register_2 (.D(former), .Q(latter), .clk(CLK), .clr(eq));  // open: en
  Comparator #(.width(3), .mode("unsigned")) comparator_2 (.a(in_1), .b(CLK_res), .eq(eq));  // open: gt, lt
  Register #(.width(4)) register_3 (.D(former), .Q(out_2), .clk(eq));  // open: en, clr

  // Other names for the same wires on the sheet: in[2:0] = in_1
endmodule
