// Logisim project fib_test.circ as structural Verilog: 1 circuit, main circuit main
module main (
  output [3:0] out_1,
  output out_2
);

  wire clock_1_out;

  Counter #(.width(6), .max('h3f)) counter_1 (.carry(out_2), .clk(clock_1_out));  // open: load, D, count, Q, clr
  Clock clock_1 (.out(clock_1_out));
  Register #(.width(4)) register_1 (.Q(out_1), .clk(out_2));  // open: D, en, clr
endmodule
