// Logisim project ftoi.circ as structural Verilog
module ftoi (
  input  [15:0] float,
  output [31:0] \int 
);

  wire and_1_out, and_2_out, not_1_out, not_2_out, not_3_out, not_4_out, not_5_out, or_1_out;
  wire [31:0] normalized_1_result;

  Normalized normalized_1 (.float(float), .result(normalized_1_result));
  Multiplexer #(.width(32)) multiplexer_1 (
    .in0(normalized_1_result), .in1({32{1'b0}}), .out(\int ), .sel(or_1_out));  // open: en
  or or_1 (or_1_out, and_2_out, and_1_out);
  and and_1 (and_1_out, float[10], float[11], float[12], float[13], float[14]);
  not not_1 (not_1_out, float[10]);
  not not_2 (not_2_out, float[11]);
  and and_2 (and_2_out, not_1_out, not_2_out, not_3_out, not_4_out, not_5_out);
  not not_3 (not_3_out, float[12]);
  not not_4 (not_4_out, float[13]);
  not not_5 (not_5_out, float[14]);

  // Other names for the same wires on the sheet: _5 = float[10]; _4 = float[11]; _3 = float[12]; _2 = float[13];
  //   _1 = float[14]
endmodule

// ll
module Normalized (
  input  [15:0] float,
  output [31:0] result
);

  wire [4:0] subtractor_1_out;
  wire [31:0] adder_1_out, logicalshift_1_result, not_1_out;

  Subtractor #(.width(5)) subtractor_1 (.a(float[14:10]), .b(5'b01111), .out(subtractor_1_out));  // open: bin, bout
  // Probe on subtractor_1_out
  LogicalShift logicalshift_1 (.num({22'h1, float[9:0]}), .shift(subtractor_1_out), .result(logicalshift_1_result));
  // Probe on {22'h1, float[9:0]}
  // Probe on {22'h1, float[9:0]}
  assign not_1_out = ~logicalshift_1_result;  // NOT_Gate not_1, 32 bits wide
  Adder #(.width(32)) adder_1 (.a(not_1_out), .b(32'h1), .out(adder_1_out));  // open: cin, cout
  Multiplexer #(.width(32)) multiplexer_1 (
    .in0(logicalshift_1_result), .in1(adder_1_out), .out(result), .sel(float[15]));  // open: en

  // Other names for the same wires on the sheet: exp[4:0] = float[14:10]; sgn = float[15]; num[9:0] = float[9:0]
endmodule

module LogicalShift (
  input  [31:0] num,
  input  [4:0] shift,
  output [31:0] result
);

  wire [9:0] multiplexer_5_out;
  wire [31:0] multiplexer_1_out, multiplexer_2_out, multiplexer_3_out, multiplexer_4_out;

  Multiplexer #(.width(32)) multiplexer_1 (
    .in0(num), .in1({num[30:0], 1'b0}), .out(multiplexer_1_out), .sel(shift[0]));  // open: en
  Multiplexer #(.width(32)) multiplexer_2 (
    .in0(multiplexer_1_out), .in1({multiplexer_1_out[29:0], 2'b00}), .out(multiplexer_2_out), .sel(shift[1]));  // open: en
  Multiplexer #(.width(32)) multiplexer_3 (
    .in0(multiplexer_2_out), .in1({multiplexer_2_out[27:0], 4'b0000}), .out(multiplexer_3_out), .sel(shift[2]));  // open: en
  Multiplexer #(.width(32)) multiplexer_4 (
    .in0(multiplexer_3_out), .in1({multiplexer_3_out[23:0], {8{1'b0}}}), .out(multiplexer_4_out),
    .sel(shift[3]));  // open: en
  Multiplexer #(.width(32)) multiplexer_5 (
    .in0(multiplexer_4_out), .in1({32{1'b0}}), .out({result[21:0], multiplexer_5_out}), .sel(shift[4]));  // open: en

  assign result[31:22] = {10{1'b0}};
endmodule
