// Logisim project mod5.circ as structural Verilog: 1 circuit, main circuit mod5
module mod5 (
  input  In,
  output s0,
  output s1,
  output s2,
  output s3,
  output s4
);

  wire clock_1_out, not_in, not_st, st;

  not not_1 (not_in, In);
  Clock clock_1 (.out(clock_1_out));
  Register #(.width(1)) register_1 (.D(In), .Q(st), .clk(clock_1_out));  // open: en, clr
  not not_2 (not_st, st);
  and and_1 (s1, not_in, not_st);
  and and_2 (s2, In, not_st);
  and and_3 (s3, In, st);
  and and_4 (s4, not_in, st);

  assign s0 = 1'b0;
endmodule
