// Logisim project navigation.circ as structural Verilog
module navigation (
  input  [1:0] dir,
  input  clk,
  input  reset,
  output arrive,
  output hit
);

  wire and_1_out, and_3_out, and_4_out, and_5_out, and_7_out, and_8_out, and_9_out, and_10_out, I0, I1, I2,
       I3, I4, I5, I6, I7, I8, nM0, nM1, not_3_out, not_4_out, not_5_out, not_6_out, not_7_out, not_8_out,
       not_9_out, not_10_out, not_11_out, O0, O1, O2, O3, O4, O5, O6, O7, or_1_out, or_2_out, or_3_out,
       or_4_out, or_5_out, or_6_out, or_9_out, or_10_out, or_12_out, or_13_out, or_14_out, or_15_out, select,
       xnor_1_out, xor_1_out;
  wire [0:0] register_1_q;
  wire [8:0] bit_extender_2_out, multiplexer_1_out;
  wire [31:0] bit_extender_1_out, counter_1_q;

  not not_1 (nM1, dir[1]);
  not not_2 (nM0, dir[0]);
  assign bit_extender_1_out = {{31{1'b0}}, 1'b0};  // Bit_Extender bit_extender_1
  Counter #(.width(32), .max('hffffffff)) counter_1 (
    .Q(counter_1_q), .clk(clk), .clr(reset));  // open: load, D, count, carry
  or or_1 (or_1_out, O3, O2);
  and and_1 (and_1_out, or_1_out, dir[1], nM0);
  or or_2 (or_2_out, O0, O1);
  or or_3 (or_3_out, O6, O7);
  or or_4 (or_4_out, O4, O5);
  or or_5 (or_5_out, O2, O3);
  and and_2 (I4, or_5_out, nM1, dir[0]);
  or or_6 (or_6_out, O2, O3);
  Comparator #(.width(32), .mode("unsigned")) comparator_1 (
    .a(bit_extender_1_out), .b(counter_1_q), .lt(select));  // open: gt, eq
  or or_7 (I0, arrive, and_1_out);
  and and_3 (and_3_out, or_2_out, nM1, nM0);
  or or_8 (I2, and_3_out, and_4_out, and_5_out);
  and and_4 (and_4_out, or_3_out, dir[1], nM0);
  and and_5 (and_5_out, or_4_out, dir[1], dir[0]);
  and and_6 (I6, or_6_out, nM1, nM0);
  assign bit_extender_2_out = {{8{1'b0}}, 1'b1};  // Bit_Extender bit_extender_2
  or or_9 (or_9_out, O4, O5);
  and and_7 (and_7_out, or_9_out, nM1, nM0);
  or or_10 (or_10_out, O6, O7);
  and and_8 (and_8_out, or_10_out, nM1, dir[0]);
  Multiplexer #(.width(9)) multiplexer_1 (
    .in0(bit_extender_2_out), .in1({I8, I7, I6, I5, I4, I3, I2, I1, I0}), .out(multiplexer_1_out),
    .sel(select));  // open: en
  or or_11 (I8, and_7_out, and_8_out);
  Register #(.width(9)) register_1 (
    .D({I8, I7, I6, I5, I4, I3, I2, I1, I0}), .Q({arrive, O7, O6, O5, O4, O3, O2, O1, register_1_q[0]}),
    .clk(clk), .clr(reset));  // open: en
  and and_9 (and_9_out, nM1, nM0);
  or or_12 (or_12_out, O2, O3);
  and and_10 (and_10_out, dir[1], dir[0]);
  or or_13 (or_13_out, O4, O5);
  xor xor_1 (xor_1_out, dir[1], dir[0]);
  or or_14 (or_14_out, O6, O7);
  xnor xnor_1 (xnor_1_out, dir[1], dir[0]);
  not not_3 (not_3_out, O1);
  not not_4 (not_4_out, O2);
  not not_5 (not_5_out, O3);
  not not_6 (not_6_out, O4);
  and and_11 (O0, not_3_out, not_4_out, not_5_out, not_6_out, not_7_out, not_8_out, not_9_out, not_10_out);
  not not_7 (not_7_out, O5);
  not not_8 (not_8_out, O6);
  not not_9 (not_9_out, O7);
  not not_10 (not_10_out, arrive);
  or or_15 (or_15_out, O0, O1);
  and and_12 (I1, or_15_out, not_11_out);
  not not_11 (not_11_out, and_9_out);
  and and_13 (I3, or_12_out, and_10_out);
  and and_14 (I5, or_13_out, xor_1_out);
  and and_15 (I7, or_14_out, xnor_1_out);
  or or_16 (hit, O1, O3, O5, O7);

  // Other names for the same wires on the sheet: O8 = arrive; M0 = dir[0]; M1 = dir[1]
endmodule
