// Logisim project CPU.circ as structural Verilog: 12 circuits, main circuit main
module main (
  input  Reset,
  output [31:0] out_2,
  output out_3,
  output [4:0] out_4,
  output [31:0] RegData,
  output out_6,
  output [4:0] MemAddr,
  output [31:0] MemData
);

  wire ALUSrc, and_1_out, Branch, clk, MemtoReg, RegDst, ShiftSel, Signed, Zero;
  wire [1:0] ALUOp, RegWriteSel;
  wire [4:0] multiplexer_4_out, rd, rs, rt, Shamt;
  wire [5:0] Funct, OpCode;
  wire [15:0] imm16;
  wire [31:0] adder_1_out, adder_2_out, alu_1_out, dm_1_dataout, grf_1_rd1, imm32, multiplexer_3_out,
       multiplexer_5_out, NextPC, PC, shifter_1_out, shiftleft2_1_out;

  // Probe on OpCode
  Clock clock_1 (.out(clk));
  // Probe on out_2
  IFU ifu_1 (
    .NPC(NextPC), .Reset(Reset), .clk(clk), .OpCode(OpCode), .Func(Funct), .PC(PC), .Instr(out_2), .rs(rs),
    .rt(rt), .rd(rd), .Shamt(Shamt), .imm16(imm16));
  // Probe on Funct
  CPU_Control cpu_control_1 (
    .Funct(Funct), .OpCode(OpCode), .RegDst(RegDst), .RegWrite(out_3), .ALUOp(ALUOp), .ALUSrc(ALUSrc),
    .MemtoReg(MemtoReg), .MemWrite(out_6), .Branch(Branch), .RegWriteSel(RegWriteSel), .ShiftSel(ShiftSel),
    .Signed(Signed));
  Adder #(.width(32)) adder_1 (.a(32'h4), .b(PC), .out(adder_1_out));  // open: cin, cout
  Multiplexer #(.width(5)) multiplexer_1 (.in0(rt), .in1(rd), .out(out_4), .sel(RegDst));  // open: en
  // Probe on out_4
  ShiftLeft2 shiftleft2_1 (.in(imm32), .Out(shiftleft2_1_out));
  GRF grf_1 (
    .A1(rs), .A2(rt), .A3(out_4), .WD(RegData), .WE(out_3), .clk(clk), .reset(Reset), .RD1(grf_1_rd1),
    .RD2(MemData));
  SignExt signext_1 (.in(imm16), .Signed(Signed), .Out(imm32));
  Adder #(.width(32)) adder_2 (.a(adder_1_out), .b(shiftleft2_1_out), .out(adder_2_out));  // open: cin, cout
  // Probe on grf_1_rd1
  Multiplexer #(.width(32)) multiplexer_2 (
    .in0(adder_1_out), .in1(adder_2_out), .out(NextPC), .sel(and_1_out));  // open: en
  and and_1 (and_1_out, Zero, Branch);
  // Probe on multiplexer_5_out
  Multiplexer #(.width(32)) multiplexer_3 (
    .in0(MemData), .in1(imm32), .out(multiplexer_3_out), .sel(ShiftSel));  // open: en
  Multiplexer #(.width(5)) multiplexer_4 (
    .in0(Shamt), .in1(5'b10000), .out(multiplexer_4_out), .sel(ShiftSel));  // open: en
  ALU alu_1 (.in0(grf_1_rd1), .in1(multiplexer_5_out), .ALUOp(ALUOp), .Zero(Zero), .Out(alu_1_out));
  Multiplexer #(.width(32)) multiplexer_5 (
    .in0(MemData), .in1(imm32), .out(multiplexer_5_out), .sel(ALUSrc));  // open: en
  Multiplexer #(.select(2), .width(32)) multiplexer_6 (
    .in0(alu_1_out), .in1(dm_1_dataout), .in2(shifter_1_out), .out(RegData), .sel(RegWriteSel));  // open: in3, en
  Shifter #(.width(32)) shifter_1 (.in(multiplexer_3_out), .\dist (multiplexer_4_out), .out(shifter_1_out));
  // Probe on MemData
  // Probe on MemAddr
  Addr32to5 addr32to5_1 (.Addr32(alu_1_out), .Addr5(MemAddr));
  DM dm_1 (.AddrIn(MemAddr), .DataIn(MemData), .MemWrite(out_6), .clk(clk), .Reset(Reset), .DataOut(dm_1_dataout));
  // Probe on rs
  // Probe on rt
  // Probe on rd
  // Probe on imm32
  // Probe on RegData

  // Other names for the same wires on the sheet: GPR_rt[31:0] = MemData; instr[31:0] = out_2; MemWrite = out_6;
  //   RegAddr[4:0] = out_4; RegWrite = out_3; WD[31:0] = RegData
endmodule

module ALU (
  input  [1:0] ALUOp,
  input  [31:0] in0,
  input  [31:0] in1,
  output Zero,
  output [31:0] Out
);

  wire [31:0] adder_1_out, or_1_out, subtractor_1_out;

  Adder #(.width(32)) adder_1 (.a(in0), .b(in1), .out(adder_1_out));  // open: cin, cout
  Subtractor #(.width(32)) subtractor_1 (.a(in0), .b(in1), .out(subtractor_1_out));  // open: bin, bout
  assign or_1_out = in0 | in1;  // OR_Gate or_1, 32 bits wide
  Multiplexer #(.select(2), .width(32)) multiplexer_1 (
    .in0(adder_1_out), .in1(subtractor_1_out), .in2(or_1_out), .out(Out), .sel(ALUOp));  // open: in3, en
  Comparator #(.width(32)) comparator_1 (.a({32{1'b0}}), .b(subtractor_1_out), .eq(Zero));  // open: gt, lt
endmodule

module SignExt (
  input  [15:0] in,
  input  Signed,
  output [31:0] Out
);

  and and_1 (Out[31], in[15], Signed);

  assign Out[30:0] = {{15{Out[31]}}, in};
endmodule

// Controller
module CPU_Control (
  input  [5:0] Funct,
  input  [5:0] OpCode,
  output RegDst,
  output RegWrite,
  output [1:0] ALUOp,
  output ALUSrc,
  output MemtoReg,
  output MemWrite,
  output Branch,
  output [1:0] RegWriteSel,
  output ShiftSel,
  output Signed
);

  wire ctrl_and_logic_1_addu, ctrl_and_logic_1_beq, ctrl_and_logic_1_lui, ctrl_and_logic_1_lw,
       ctrl_and_logic_1_ori, ctrl_and_logic_1_sll, ctrl_and_logic_1_subu, ctrl_and_logic_1_sw;

  // Probe on OpCode
  // Probe on Funct
  Ctrl_AND_Logic ctrl_and_logic_1 (
    .OpCode(OpCode), .Funct(Funct), .addu(ctrl_and_logic_1_addu), .subu(ctrl_and_logic_1_subu),
    .ori(ctrl_and_logic_1_ori), .lw(ctrl_and_logic_1_lw), .sw(ctrl_and_logic_1_sw),
    .beq(ctrl_and_logic_1_beq), .lui(ctrl_and_logic_1_lui), .sll(ctrl_and_logic_1_sll));
  Ctrl_OR_Logic ctrl_or_logic_1 (
    .addu(ctrl_and_logic_1_addu), .subu(ctrl_and_logic_1_subu), .ori(ctrl_and_logic_1_ori),
    .lw(ctrl_and_logic_1_lw), .sw(ctrl_and_logic_1_sw), .beq(ctrl_and_logic_1_beq),
    .lui(ctrl_and_logic_1_lui), .sll(ctrl_and_logic_1_sll), .RegDst(RegDst), .RegWrite(RegWrite),
    .ALUOp(ALUOp), .ALUSrc(ALUSrc), .MemtoReg(MemtoReg), .MemWrite(MemWrite), .Branch(Branch),
    .RegWriteSel(RegWriteSel), .ShiftSel(ShiftSel), .Signed(Signed));
endmodule

// AND
module Ctrl_AND_Logic (
  input  [5:0] OpCode,
  input  [5:0] Funct,
  output addu,
  output subu,
  output ori,
  output lw,
  output sw,
  output beq,
  output lui,
  output sll
);

  wire _000000, nfun0, nfun1, nfun2, nfun3, nfun4, nfun5, nop0, nop1, nop2, nop3, nop4, nop5;

  not not_1 (nop5, OpCode[5]);
  not not_2 (nop4, OpCode[4]);
  not not_3 (nop3, OpCode[3]);
  not not_4 (nop2, OpCode[2]);
  not not_5 (nop1, OpCode[1]);
  not not_6 (nop0, OpCode[0]);
  not not_7 (nfun4, Funct[4]);
  not not_8 (nfun5, Funct[5]);
  and and_1 (_000000, nop5, nop4, nop3, nop2, nop1, nop0);
  not not_9 (nfun3, Funct[3]);
  not not_10 (nfun1, Funct[1]);
  not not_11 (nfun2, Funct[2]);
  not not_12 (nfun0, Funct[0]);
  and and_2 (addu, _000000, Funct[5], nfun4, nfun3, nfun2, nfun1, Funct[0]);
  and and_3 (subu, _000000, Funct[5], nfun4, nfun3, nfun2, Funct[1], Funct[0]);
  and and_4 (ori, nop5, nop4, OpCode[3], OpCode[2], nop1, OpCode[0]);
  and and_5 (lw, OpCode[5], nop4, nop3, nop2, OpCode[1], OpCode[0]);
  and and_6 (sw, OpCode[5], nop4, OpCode[3], nop2, OpCode[1], OpCode[0]);
  and and_7 (beq, nop5, nop4, nop3, OpCode[2], nop1, nop0);
  and and_8 (lui, nop5, nop4, OpCode[3], OpCode[2], OpCode[1], OpCode[0]);
  and and_9 (sll, _000000, nfun5, nfun4, nfun3, nfun2, nfun1, nfun0);

  // Other names for the same wires on the sheet: fun0 = Funct[0]; fun1 = Funct[1]; fun2 = Funct[2]; fun3 = Funct[3];
  //   fun4 = Funct[4]; fun5 = Funct[5]; op0 = OpCode[0]; op1 = OpCode[1]; op2 = OpCode[2]; op3 = OpCode[3];
  //   op4 = OpCode[4]; op5 = OpCode[5]
endmodule

// OR
module Ctrl_OR_Logic (
  input  addu,
  input  subu,
  input  ori,
  input  lw,
  input  sw,
  input  beq,
  input  lui,
  input  sll,
  output RegDst,
  output RegWrite,
  output [1:0] ALUOp,
  output ALUSrc,
  output MemtoReg,
  output MemWrite,
  output Branch,
  output [1:0] RegWriteSel,
  output ShiftSel,
  output Signed
);

  or or_1 (RegDst, addu, subu, sll);
  or or_2 (RegWrite, addu, subu, ori, lw, lui, sll);
  or or_3 (ALUSrc, ori, lw, sw);
  or or_4 (RegWriteSel[1], lui, sll);
  or or_5 (Signed, sw, lw);

  assign ALUOp = {ori, subu};
  assign Branch = beq;
  assign MemtoReg = lw;
  assign MemWrite = sw;
  assign RegWriteSel[0] = lw;
  assign ShiftSel = lui;
endmodule

// LShift16
module ShiftLeft16 (
  input  [15:0] in,
  output [31:0] out
);


  assign out = {in, {16{1'b0}}};
endmodule

module IFU (
  input  Reset,
  input  [31:0] NPC,
  input  clk,
  output [31:0] PC,
  output [31:0] Instr,
  output [4:0] rs,
  output [4:0] rt,
  output [4:0] rd,
  output [4:0] Shamt,
  output [15:0] imm16,
  output [5:0] OpCode,
  output [5:0] Func
);

  wire [4:0] addr32to5_1_addr5;

  Register #(.width(32)) u_PC (.D(NPC), .Q(PC), .clk(clk), .clr(Reset));  // open: en
  Addr32to5 addr32to5_1 (.Addr32(PC), .Addr5(addr32to5_1_addr5));
  ROM #(.addrWidth(5), .dataWidth(32)) rom_1 (
    .addr(addr32to5_1_addr5), .data({Instr[31:16], imm16[15:6], Func}));  // open: sel

  assign imm16[5:0] = Func;
  assign Instr[15:0] = {imm16[15:6], Func};
  assign OpCode = Instr[31:26];
  assign rd = imm16[15:11];
  assign rs = Instr[25:21];
  assign rt = Instr[20:16];
  assign Shamt = imm16[10:6];

  // Notes on the sheet:
  //   contents of rom_1 (hex, n*v repeats v):
  //   3c010001 34215f90 3c02ffff 3442ffff 3c037fff 3463ffff 3c040118 34846220 34050003 245021 225821
  //   416021 426821 21a023 42a823 25b023 a4b823 82c023
endmodule

module ShiftLeft2 (
  input  [31:0] in,
  output [31:0] Out
);


  assign Out = {in[29:0], 2'b00};
endmodule

module DM (
  input  [4:0] AddrIn,
  input  [31:0] DataIn,
  input  MemWrite,
  input  clk,
  input  Reset,
  output [31:0] DataOut
);

  RAM #(.addrWidth(5), .dataWidth(32), .bus("separate")) ram_1 (
    .addr(AddrIn), .din(DataIn), .data(DataOut), .str(MemWrite), .clk(clk), .clr(Reset));  // open: sel, ld
endmodule

// 32to5
module Addr32to5 (
  input  [31:0] Addr32,
  output [4:0] Addr5
);


  assign Addr5 = Addr32[6:2];
endmodule

module GRF (
  input  WE,
  input  [4:0] A1,
  input  [4:0] A2,
  input  [4:0] A3,
  input  [31:0] WD,
  input  clk,
  input  reset,
  output [31:0] RD1,
  output [31:0] RD2
);

  wire and_1_out, and_2_out, and_3_out, and_4_out, and_5_out, and_6_out, and_7_out, and_8_out, and_9_out,
       and_10_out, and_11_out, and_12_out, and_13_out, and_14_out, and_15_out, and_16_out, and_17_out,
       and_18_out, and_19_out, and_20_out, and_21_out, and_22_out, and_23_out, and_24_out, and_25_out,
       and_26_out, and_27_out, and_28_out, and_29_out, and_30_out, and_31_out, and_32_out, Sel0, Sel1, Sel2,
       Sel3, Sel4, Sel5, Sel6, Sel7, Sel8, Sel9, Sel10, Sel11, Sel12, Sel13, Sel14, Sel15, Sel16, Sel17,
       Sel18, Sel19, Sel20, Sel21, Sel22, Sel23, Sel24, Sel25, Sel26, Sel27, Sel28, Sel29, Sel30, Sel31;
  wire [31:0] multiplexer_1_out, multiplexer_2_out, multiplexer_3_out, multiplexer_4_out, multiplexer_5_out,
       multiplexer_6_out, multiplexer_7_out, multiplexer_8_out, multiplexer_9_out, multiplexer_10_out,
       multiplexer_11_out, multiplexer_12_out, multiplexer_13_out, multiplexer_14_out, multiplexer_15_out,
       multiplexer_16_out, multiplexer_17_out, multiplexer_18_out, multiplexer_19_out, multiplexer_20_out,
       multiplexer_21_out, multiplexer_22_out, multiplexer_23_out, multiplexer_24_out, multiplexer_25_out,
       multiplexer_26_out, multiplexer_27_out, multiplexer_28_out, multiplexer_29_out, multiplexer_30_out,
       multiplexer_31_out, multiplexer_32_out, O0, O1, O2, O3, O4, O5, O6, O7, O8, O9, O10, O11, O12, O13,
       O14, O15, O16, O17, O18, O19, O20, O21, O22, O23, O24, O25, O26, O27, O28, O29, O30, O31;

  Register #(.width(32)) _0 (.D(multiplexer_1_out), .Q(O0), .clk(clk), .clr(reset));  // open: en
  Multiplexer #(.width(32)) multiplexer_1 (.in0(O0), .in1(WD), .out(multiplexer_1_out), .sel(and_1_out));  // open: en
  and and_1 (and_1_out, WE, 1'b0, Sel0);
  Register #(.width(32)) _1 (.D(multiplexer_2_out), .Q(O1), .clk(clk), .clr(reset));  // open: en
  Multiplexer #(.width(32)) multiplexer_2 (.in0(O1), .in1(WD), .out(multiplexer_2_out), .sel(and_2_out));  // open: en
  and and_2 (and_2_out, WE, Sel1);
  Register #(.width(32)) _2 (.D(multiplexer_3_out), .Q(O2), .clk(clk), .clr(reset));  // open: en
  Multiplexer #(.width(32)) multiplexer_3 (.in0(O2), .in1(WD), .out(multiplexer_3_out), .sel(and_3_out));  // open: en
  and and_3 (and_3_out, WE, Sel2);
  Register #(.width(32)) _3 (.D(multiplexer_4_out), .Q(O3), .clk(clk), .clr(reset));  // open: en
  Multiplexer #(.width(32)) multiplexer_4 (.in0(O3), .in1(WD), .out(multiplexer_4_out), .sel(and_4_out));  // open: en
  and and_4 (and_4_out, WE, Sel3);
  Multiplexer #(.width(32)) multiplexer_5 (.in0(O4), .in1(WD), .out(multiplexer_5_out), .sel(and_5_out));  // open: en
  Register #(.width(32)) _4 (.D(multiplexer_5_out), .Q(O4), .clk(clk), .clr(reset));  // open: en
  and and_5 (and_5_out, WE, Sel4);
  Register #(.width(32)) _5 (.D(multiplexer_6_out), .Q(O5), .clk(clk), .clr(reset));  // open: en
  Multiplexer #(.width(32)) multiplexer_6 (.in0(O5), .in1(WD), .out(multiplexer_6_out), .sel(and_6_out));  // open: en
  and and_6 (and_6_out, WE, Sel5);
  Register #(.width(32)) _6 (.D(multiplexer_7_out), .Q(O6), .clk(clk), .clr(reset));  // open: en
  Multiplexer #(.width(32)) multiplexer_7 (.in0(O6), .in1(WD), .out(multiplexer_7_out), .sel(and_7_out));  // open: en
  and and_7 (and_7_out, WE, Sel6);
  Register #(.width(32)) _7 (.D(multiplexer_8_out), .Q(O7), .clk(clk), .clr(reset));  // open: en
  Multiplexer #(.width(32)) multiplexer_8 (.in0(O7), .in1(WD), .out(multiplexer_8_out), .sel(and_8_out));  // open: en
  and and_8 (and_8_out, WE, Sel7);
  Multiplexer #(.width(32)) multiplexer_9 (.in0(O8), .in1(WD), .out(multiplexer_9_out), .sel(and_9_out));  // open: en
  and and_9 (and_9_out, WE, Sel8);
  Multiplexer #(.width(32)) multiplexer_10 (
    .in0(O9), .in1(WD), .out(multiplexer_10_out), .sel(and_10_out));  // open: en
  and and_10 (and_10_out, WE, Sel9);
  Multiplexer #(.width(32)) multiplexer_11 (
    .in0(O10), .in1(WD), .out(multiplexer_11_out), .sel(and_11_out));  // open: en
  and and_11 (and_11_out, WE, Sel10);
  Multiplexer #(.width(32)) multiplexer_12 (
    .in0(O11), .in1(WD), .out(multiplexer_12_out), .sel(and_12_out));  // open: en
  and and_12 (and_12_out, WE, Sel11);
  Multiplexer #(.width(32)) multiplexer_13 (
    .in0(O12), .in1(WD), .out(multiplexer_13_out), .sel(and_13_out));  // open: en
  and and_13 (and_13_out, WE, Sel12);
  Multiplexer #(.width(32)) multiplexer_14 (
    .in0(O13), .in1(WD), .out(multiplexer_14_out), .sel(and_14_out));  // open: en
  and and_14 (and_14_out, WE, Sel13);
  Multiplexer #(.width(32)) multiplexer_15 (
    .in0(O14), .in1(WD), .out(multiplexer_15_out), .sel(and_15_out));  // open: en
  and and_15 (and_15_out, WE, Sel14);
  Multiplexer #(.width(32)) multiplexer_16 (
    .in0(O15), .in1(WD), .out(multiplexer_16_out), .sel(and_16_out));  // open: en
  and and_16 (and_16_out, WE, Sel15);
  Register #(.width(32)) _8 (.D(multiplexer_9_out), .Q(O8), .clk(clk), .clr(reset));  // open: en
  Register #(.width(32)) _9 (.D(multiplexer_10_out), .Q(O9), .clk(clk), .clr(reset));  // open: en
  Register #(.width(32)) _10 (.D(multiplexer_11_out), .Q(O10), .clk(clk), .clr(reset));  // open: en
  Register #(.width(32)) _11 (.D(multiplexer_12_out), .Q(O11), .clk(clk), .clr(reset));  // open: en
  Register #(.width(32)) _12 (.D(multiplexer_13_out), .Q(O12), .clk(clk), .clr(reset));  // open: en
  Register #(.width(32)) _13 (.D(multiplexer_14_out), .Q(O13), .clk(clk), .clr(reset));  // open: en
  Register #(.width(32)) _14 (.D(multiplexer_15_out), .Q(O14), .clk(clk), .clr(reset));  // open: en
  Register #(.width(32)) _15 (.D(multiplexer_16_out), .Q(O15), .clk(clk), .clr(reset));  // open: en
  Multiplexer #(.width(32)) multiplexer_17 (
    .in0(O16), .in1(WD), .out(multiplexer_17_out), .sel(and_17_out));  // open: en
  and and_17 (and_17_out, WE, Sel16);
  Multiplexer #(.width(32)) multiplexer_18 (
    .in0(O17), .in1(WD), .out(multiplexer_18_out), .sel(and_18_out));  // open: en
  and and_18 (and_18_out, WE, Sel17);
  Multiplexer #(.width(32)) multiplexer_19 (
    .in0(O18), .in1(WD), .out(multiplexer_19_out), .sel(and_19_out));  // open: en
  and and_19 (and_19_out, WE, Sel18);
  Multiplexer #(.width(32)) multiplexer_20 (
    .in0(O19), .in1(WD), .out(multiplexer_20_out), .sel(and_20_out));  // open: en
  and and_20 (and_20_out, WE, Sel19);
  Multiplexer #(.width(32)) multiplexer_21 (
    .in0(O20), .in1(WD), .out(multiplexer_21_out), .sel(and_21_out));  // open: en
  and and_21 (and_21_out, WE, Sel20);
  Multiplexer #(.width(32)) multiplexer_22 (
    .in0(O21), .in1(WD), .out(multiplexer_22_out), .sel(and_22_out));  // open: en
  and and_22 (and_22_out, WE, Sel21);
  Multiplexer #(.width(32)) multiplexer_23 (
    .in0(O22), .in1(WD), .out(multiplexer_23_out), .sel(and_23_out));  // open: en
  and and_23 (and_23_out, WE, Sel22);
  Multiplexer #(.width(32)) multiplexer_24 (
    .in0(O23), .in1(WD), .out(multiplexer_24_out), .sel(and_24_out));  // open: en
  and and_24 (and_24_out, WE, Sel23);
  Register #(.width(32)) _16 (.D(multiplexer_17_out), .Q(O16), .clk(clk), .clr(reset));  // open: en
  Register #(.width(32)) _17 (.D(multiplexer_18_out), .Q(O17), .clk(clk), .clr(reset));  // open: en
  Register #(.width(32)) _18 (.D(multiplexer_19_out), .Q(O18), .clk(clk), .clr(reset));  // open: en
  Register #(.width(32)) _19 (.D(multiplexer_20_out), .Q(O19), .clk(clk), .clr(reset));  // open: en
  Register #(.width(32)) _20 (.D(multiplexer_21_out), .Q(O20), .clk(clk), .clr(reset));  // open: en
  Register #(.width(32)) _21 (.D(multiplexer_22_out), .Q(O21), .clk(clk), .clr(reset));  // open: en
  Register #(.width(32)) _22 (.D(multiplexer_23_out), .Q(O22), .clk(clk), .clr(reset));  // open: en
  Register #(.width(32)) _23 (.D(multiplexer_24_out), .Q(O23), .clk(clk), .clr(reset));  // open: en
  Multiplexer #(.width(32)) multiplexer_25 (
    .in0(O24), .in1(WD), .out(multiplexer_25_out), .sel(and_25_out));  // open: en
  and and_25 (and_25_out, WE, Sel24);
  Multiplexer #(.width(32)) multiplexer_26 (
    .in0(O25), .in1(WD), .out(multiplexer_26_out), .sel(and_26_out));  // open: en
  and and_26 (and_26_out, WE, Sel25);
  Multiplexer #(.width(32)) multiplexer_27 (
    .in0(O26), .in1(WD), .out(multiplexer_27_out), .sel(and_27_out));  // open: en
  and and_27 (and_27_out, WE, Sel26);
  Multiplexer #(.width(32)) multiplexer_28 (
    .in0(O27), .in1(WD), .out(multiplexer_28_out), .sel(and_28_out));  // open: en
  and and_28 (and_28_out, WE, Sel27);
  Multiplexer #(.width(32)) multiplexer_29 (
    .in0(O28), .in1(WD), .out(multiplexer_29_out), .sel(and_29_out));  // open: en
  and and_29 (and_29_out, WE, Sel28);
  Multiplexer #(.width(32)) multiplexer_30 (
    .in0(O29), .in1(WD), .out(multiplexer_30_out), .sel(and_30_out));  // open: en
  and and_30 (and_30_out, WE, Sel29);
  Multiplexer #(.width(32)) multiplexer_31 (
    .in0(O30), .in1(WD), .out(multiplexer_31_out), .sel(and_31_out));  // open: en
  and and_31 (and_31_out, WE, Sel30);
  Multiplexer #(.width(32)) multiplexer_32 (
    .in0(O31), .in1(WD), .out(multiplexer_32_out), .sel(and_32_out));  // open: en
  and and_32 (and_32_out, WE, Sel31);
  Register #(.width(32)) _24 (.D(multiplexer_25_out), .Q(O24), .clk(clk), .clr(reset));  // open: en
  Register #(.width(32)) _25 (.D(multiplexer_26_out), .Q(O25), .clk(clk), .clr(reset));  // open: en
  Register #(.width(32)) _26 (.D(multiplexer_27_out), .Q(O26), .clk(clk), .clr(reset));  // open: en
  Register #(.width(32)) _27 (.D(multiplexer_28_out), .Q(O27), .clk(clk), .clr(reset));  // open: en
  Register #(.width(32)) _28 (.D(multiplexer_29_out), .Q(O28), .clk(clk), .clr(reset));  // open: en
  Register #(.width(32)) _29 (.D(multiplexer_30_out), .Q(O29), .clk(clk), .clr(reset));  // open: en
  Register #(.width(32)) _30 (.D(multiplexer_31_out), .Q(O30), .clk(clk), .clr(reset));  // open: en
  Register #(.width(32)) _31 (.D(multiplexer_32_out), .Q(O31), .clk(clk), .clr(reset));  // open: en
  Multiplexer #(.select(5), .width(32)) multiplexer_33 (
    .in0(O0), .in1(O1), .in2(O2), .in3(O3), .in4(O4), .in5(O5), .in6(O6), .in7(O7), .in8(O8), .in9(O9),
    .in10(O10), .in11(O11), .in12(O12), .in13(O13), .in14(O14), .in15(O15), .in16(O16), .in17(O17),
    .in18(O18), .in19(O19), .in20(O20), .in21(O21), .in22(O22), .in23(O23), .in24(O24), .in25(O25),
    .in26(O26), .in27(O27), .in28(O28), .in29(O29), .in30(O30), .in31(O31), .out(RD1), .sel(A1));  // open: en
  Multiplexer #(.select(5), .width(32)) multiplexer_34 (
    .in0(O0), .in1(O1), .in2(O2), .in3(O3), .in4(O4), .in5(O5), .in6(O6), .in7(O7), .in8(O8), .in9(O9),
    .in10(O10), .in11(O11), .in12(O12), .in13(O13), .in14(O14), .in15(O15), .in16(O16), .in17(O17),
    .in18(O18), .in19(O19), .in20(O20), .in21(O21), .in22(O22), .in23(O23), .in24(O24), .in25(O25),
    .in26(O26), .in27(O27), .in28(O28), .in29(O29), .in30(O30), .in31(O31), .out(RD2), .sel(A2));  // open: en
  Demultiplexer #(.select(5)) demultiplexer_1 (
    .out0(Sel0), .out1(Sel1), .out2(Sel2), .out3(Sel3), .out4(Sel4), .out5(Sel5), .out6(Sel6), .out7(Sel7),
    .out8(Sel8), .out9(Sel9), .out10(Sel10), .out11(Sel11), .out12(Sel12), .out13(Sel13), .out14(Sel14),
    .out15(Sel15), .out16(Sel16), .out17(Sel17), .out18(Sel18), .out19(Sel19), .out20(Sel20), .out21(Sel21),
    .out22(Sel22), .out23(Sel23), .out24(Sel24), .out25(Sel25), .out26(Sel26), .out27(Sel27), .out28(Sel28),
    .out29(Sel29), .out30(Sel30), .out31(Sel31), .in(1'b1), .sel(A3));  // open: en

  // Other names for the same wires on the sheet: inData[31:0] = WD
endmodule
